// Logisim project Lab 2.circ as structural Verilog
module Task_1 (
  input  A,
  input  A_2,
  input  B,
  input  A_3,
  input  B_2,
  input  A_4,
  input  B_3,
  output A_prime,
  output AB,
  output A_prime_B_prime___A_B,
  output A_B__prime
);

  wire nand_2_out, nand_3_out, nand_4_out, nand_5_out, nand_6_out, nand_9_out;

  nand nand_1 (A_prime, A, A);
  nand nand_2 (nand_2_out, A_2, B);
  nand nand_3 (nand_3_out, A_3, A_3);
  nand nand_4 (nand_4_out, B_2, B_2);
  nand nand_5 (nand_5_out, A_4, A_4);
  nand nand_6 (nand_6_out, B_3, B_3);
  nand nand_7 (AB, nand_2_out, nand_2_out);
  nand nand_8 (A_prime_B_prime___A_B, nand_3_out, nand_4_out);
  nand nand_9 (nand_9_out, nand_5_out, nand_6_out);
  nand nand_10 (A_B__prime, nand_9_out, nand_9_out);

  // Notes on the sheet:
  //   (AB)'
  //   A'
  //   B'
  //   A'
  //   B'
  //   (A'B')"=A+B
endmodule

module Task_2 (
  input  A,
  input  B,
  input  A_2,
  input  B_2,
  input  A_3,
  input  B_3,
  input  A_4,
  input  B_4,
  output out_9,
  output AB__A_B__prime__prime,
  output out_11,
  output out_12
);

  wire nand_1_out, nand_2_out, nand_3_out, nand_4_out, nand_5_out, nand_6_out, nand_8_out, nor_1_out,
       nor_2_out, nor_3_out, nor_4_out, nor_5_out, nor_6_out, nor_7_out;

  nand nand_1 (nand_1_out, A, B);
  nand nand_2 (nand_2_out, A_3, B_3);
  nor nor_1 (nor_1_out, A_4, B_4);
  nand nand_3 (nand_3_out, A, nand_1_out);
  nand nand_4 (nand_4_out, nand_1_out, B);
  nor nor_2 (nor_2_out, A_2, A_2);
  nor nor_3 (nor_3_out, B_2, B_2);
  nor nor_4 (nor_4_out, B_2, A_2);
  nand nand_5 (nand_5_out, A_3, nand_2_out);
  nand nand_6 (nand_6_out, nand_2_out, B_3);
  nor nor_5 (nor_5_out, A_4, nor_1_out);
  nor nor_6 (nor_6_out, nor_1_out, B_4);
  nand nand_7 (out_9, nand_3_out, nand_4_out);
  nor nor_7 (nor_7_out, nor_2_out, nor_3_out);
  nand nand_8 (nand_8_out, nand_5_out, nand_6_out);
  nor nor_8 (out_12, nor_5_out, nor_6_out);
  nor nor_9 (AB__A_B__prime__prime, nor_7_out, nor_4_out);
  nand nand_9 (out_11, nand_8_out, nand_8_out);

  // Notes on the sheet:
  //   XOR Using NAND
  //   XOR Using Nor
  //   XNOR Using NAND
  //   XNOR Using XOR
  //   (AB)'
  //   (AB)'
  //   (A+B)'
  //   (A.(AB)')'=A'+AB
  //   (A+A)'=A'
  //   (B+B)'=B'
  //   (A+B)'
  //   (A.(AB)')'
  //   (A+(A+B)')'
  //   (B.(AB)')'=B'+AB
  //   (B.(AB)')'
  //   (B+(A+B)')'
  //   ((A'+AB).(B'+AB))'
  //   ((A(AB)')'.(B(AB)')')'
  //   ((A+(A+B)')'+(B+(A+B)')')'
  //   (A'+B')' = AB
  //   (A(AB)')'.(B(AB)')'
endmodule

module Task_3 (
  input  A,
  input  B,
  input  C,
  output AC_BC_prime
);

  wire ic7404_1_out_8, ic7408_1_out_11, ic7408_1_out_12;

  ic7404 ic7404_1 (.in_4(C), .out_8(ic7404_1_out_8));  // open: in_1, in_2, in_3, out_5, out_6, out_7
  ic7408 ic7408_1 (
    .in_5(ic7404_1_out_8), .in_6(B), .in_7(C), .in_8(A), .out_11(ic7408_1_out_11), .out_12(ic7408_1_out_12));  // open: in_1, in_2, in_3, in_4, out_9, out_10
  ic7432 ic7432_1 (
    .in_7(ic7408_1_out_11), .in_8(ic7408_1_out_12), .out_12(AC_BC_prime));  // open: in_1, in_2, in_3, in_4, in_5, in_6, out_9, out_10, out_11

  // Notes on the sheet:
  //   C'
  //   AC
  //   BC'
endmodule

module ic7408 (
  input  in_1,
  input  in_2,
  input  in_3,
  input  in_4,
  input  in_5,
  input  in_6,
  input  in_7,
  input  in_8,
  output out_9,
  output out_10,
  output out_11,
  output out_12
);

  and and_1 (out_9, in_1, in_2);
  and and_2 (out_10, in_3, in_4);
  and and_3 (out_11, in_5, in_6);
  and and_4 (out_12, in_7, in_8);
endmodule

module ic7432 (
  input  in_1,
  input  in_2,
  input  in_3,
  input  in_4,
  input  in_5,
  input  in_6,
  input  in_7,
  input  in_8,
  output out_9,
  output out_10,
  output out_11,
  output out_12
);

  or or_1 (out_9, in_1, in_2);
  or or_2 (out_10, in_3, in_4);
  or or_3 (out_11, in_5, in_6);
  or or_4 (out_12, in_7, in_8);
endmodule

module ic7404 (
  input  in_1,
  input  in_2,
  input  in_3,
  input  in_4,
  output out_5,
  output out_6,
  output out_7,
  output out_8
);

  not not_1 (out_5, in_1);
  not not_2 (out_6, in_2);
  not not_3 (out_7, in_3);
  not not_4 (out_8, in_4);
endmodule
